# Fritzing sketch motion-light (saved by Fritzing 0.9.3b)
circuit board: 2.83718cm x 3.45693cm
circuit board: 2.83718cm x 3.45693cm
circuit board: 2.83718cm x 3.45693cm
breadboards: 1

parts:
  HLK-PM1 = HLK-PM01
  U1 = RELAY [part_number="TIANBO HJR-3FF-S-H" package=OJ]
  Q1 = TRANSISTOR_NPN [package=to-92-ammo]
  D1 = Diode [package=diode-1n4001]
  WeMos_D1_Mini1 = WeMos D1 Mini
  J3 = female pin header, 8 pins [form="♀ (female)"]  # not connected
  J5 = female pin header, 8 pins [form="♀ (female)"]  # not connected
  J6 = female pin header, 8 pins [form="♀ (female)"]  # not connected
  J8 = female pin header, 4 pins [form="♀ (female)"]
  J7 = female pin header, 8 pins [form="♀ (female)"]  # not connected
  R2 = Resistor [tolerance=±5% resistance=470 package=THT]
  R1 = Resistor [tolerance=±5% resistance=4.7k package=THT]

nets:
  N1: HLK-PM1.-Vo, Q1.E, WeMos_D1_Mini1.G, J8.pin2
  N2: HLK-PM1.+Vo, U1.COIL2, D1.C, WeMos_D1_Mini1.5V, J8.pin1
  N3: U1.COIL1, Q1.C, D1.A
  N4: Q1.B, R2.Pin_0
  N5: WeMos_D1_Mini1.3V3, R1.Pin_0
  N6: WeMos_D1_Mini1.A0, J8.pin4, R1.Pin_1
  N7: WeMos_D1_Mini1.D1, R2.Pin_1
  N8: WeMos_D1_Mini1.D2, J8.pin3
